# Fritzing sketch Collegamenti Braccio Robotico (saved by Fritzing 0.9.3b)

parts:
  ARDUINO_UNO = Arduino Uno (Rev3) - ICSP
  Polso_(Servo_1) = Basic Servo
  J2 = Dagu DGServo 9g header connector (female) [package=THT]
  Gomito_(Servo_2) = Basic Servo
  J4 = Dagu DGServo 9g header connector (female) [package=THT]
  Spalla_(Servo_3) = Basic Servo
  J6 = Dagu DGServo 9g header connector (female) [package=THT]
  Base_(Servo_4) = Basic Servo
  J8 = Dagu DGServo 9g header connector (female) [package=THT]
  Pinza_(Servo_0) = Basic Servo
  J12 = Dagu DGServo 9g header connector (female) [package=THT]
  VCC1 = Battery
  M1 = STM32407VG Discovery

nets:
  N1: ARDUINO_UNO.D0/RX, M1.PC4, M1.PA4
  N2: ARDUINO_UNO.D1/TX, M1.PC5, M1.PA7
  N3: ARDUINO_UNO.D2, Pinza_(Servo_0).pulse, J12.pulse
  N4: ARDUINO_UNO.D3_PWM, Polso_(Servo_1).pulse, J2.pulse
  N5: ARDUINO_UNO.D4, Gomito_(Servo_2).pulse, J4.pulse
  N6: ARDUINO_UNO.D5_PWM, Spalla_(Servo_3).pulse, J6.pulse
  N7: ARDUINO_UNO.D6_PWM, Base_(Servo_4).pulse, J8.pulse
  N8: ARDUINO_UNO.GND, VCC1.-
  GND: Polso_(Servo_1).gnd, J2.gnd
  VCC: Polso_(Servo_1).vcc, J2.Vcc
  GND_2: Gomito_(Servo_2).gnd, J4.gnd
  VCC_2: Gomito_(Servo_2).vcc, J4.Vcc
  GND_3: Spalla_(Servo_3).gnd, J6.gnd
  VCC_3: Spalla_(Servo_3).vcc, J6.Vcc
  GND_4: Base_(Servo_4).gnd, J8.gnd
  VCC_4: Base_(Servo_4).vcc, J8.Vcc, VCC1.+
  GND_5: Pinza_(Servo_0).gnd, J12.gnd
  VCC_5: Pinza_(Servo_0).vcc, J12.Vcc

notes:
  Alimentazione a 5v

custom parts:
  Arduino Uno (Rev3) - ICSP: The Arduino Uno is a microcontroller board based on the ATmega328 (datasheet). It has 14 digital input/output pins (of which 6 can be used as PWM outputs), 6 analog inputs, a 16 MHz ceramic resonator, a USB connection, a power jack, an ICSP header, and a reset button. It contains everything needed to support the microcontroller; simply connect it to a computer with a USB cable or power it with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
  STM32407VG Discovery: The STM32F4DISCOVERY Discovery kit allows users to easily develop applications with the STM32F407VG high performance microcontroller with the ARM® Cortex®-M4 32-bit core. It includes everything required either for beginners or for experienced users to get quickly started.Based on STM32F407VG, it includes an ST-LINK/V2 or ST-LINK/V2-A embedded debug tool, two ST-MEMS digital accelerometers, a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
